// Logisim project alu.circ as structural Verilog: 1 circuit, main circuit main
module main (
  input  [31:0] X,
  input  [31:0] Y,
  input  [3:0] Switch,
  output Signed_Overflow,
  output Equal,
  output [31:0] Result
);

  wire ADD_O, and_2_out, and_3_out, and_4_out, and_5_out, bitselector_1_out, bitselector_2_out,
       bitselector_3_out, bitselector_7_out, bitselector_8_out, bitselector_9_out, comparator_1_lt,
       comparator_2_lt, not_1_out, not_2_out, not_3_out, not_4_out, not_5_out, SLT_E, SLTU_E, SUB_O,
       xnor_1_out, xor_1_out;
  wire [4:0] bitselector_4_out, bitselector_5_out, bitselector_6_out;
  wire [31:0] ADD, ADD_X, ADD_Y, ADDU, ADDU_X, ADDU_Y, AND, AND_X, AND_Y, OR, OR_X, OR_Y, SLL, SLL_X, SLL_Y,
       SLT, SLT_X, SLT_Y, SLTU, SLTU_X, SLTU_Y, SRA, SRA_X, SRA_Y, SRL, SRL_X, SRL_Y, SUB, SUB_X, SUB_Y,
       SUBU, SUBU_X, SUBU_Y, XOR, XOR_X, XOR_Y;

  Demultiplexer #(.select(4), .width(32)) demultiplexer_1 (
    .out0(SLL_X), .out1(SRL_X), .out2(SRA_X), .out3(ADD_X), .out4(ADDU_X), .out6(SUB_X), .out7(SUBU_X),
    .out10(AND_X), .out11(OR_X), .out12(XOR_X), .out14(SLT_X), .out15(SLTU_X), .in(X), .sel(Switch));  // open: out5, out8, out9, out13, en
  Demultiplexer #(.select(4), .width(32)) demultiplexer_2 (
    .out0(SLL_Y), .out1(SRL_Y), .out2(SRA_Y), .out3(ADD_Y), .out4(ADDU_Y), .out6(SUB_Y), .out7(SUBU_Y),
    .out10(AND_Y), .out11(OR_Y), .out12(XOR_Y), .out14(SLT_Y), .out15(SLTU_Y), .in(Y), .sel(Switch));  // open: out5, out8, out9, out13, en
  Multiplexer #(.select(4)) multiplexer_1 (
    .in0(1'b0), .in1(1'b0), .in2(1'b0), .in3(ADD_O), .in4(1'b0), .in5(1'b0), .in6(SUB_O), .in7(1'b0),
    .in8(1'b0), .in9(1'b0), .in10(1'b0), .in11(1'b0), .in12(1'b0), .in13(1'b0), .in14(1'b0), .in15(1'b0),
    .out(Signed_Overflow), .sel(Switch));  // open: en
  Multiplexer #(.select(4), .width(32)) multiplexer_2 (
    .in0(SLL), .in1(SRL), .in2(SRA), .in3(ADD), .in4(ADDU), .in6(SUB), .in7(SUBU), .in10(AND), .in11(OR),
    .in12(XOR), .in14(SLT), .in15(SLTU), .out(Result), .sel(Switch));  // open: in5, in8, in9, in13, en
  Multiplexer #(.select(4)) multiplexer_3 (
    .in0(1'b0), .in1(1'b0), .in2(1'b0), .in3(1'b0), .in4(1'b0), .in5(1'b0), .in6(1'b0), .in7(1'b0),
    .in8(1'b0), .in9(1'b0), .in10(1'b0), .in11(1'b0), .in12(1'b0), .in13(SLT_E), .in14(SLT_E), .in15(SLTU_E),
    .out(Equal), .sel(Switch));  // open: en
  Subtractor #(.width(32)) subtractor_1 (.a(SUB_X), .b(SUB_Y), .out(SUB));  // open: bin, bout
  BitSelector #(.width(32)) bitselector_1 (.in(SUB_X), .out(bitselector_1_out), .sel({5{1'b1}}));
  BitSelector #(.width(32)) bitselector_2 (.in(SUB_Y), .out(bitselector_2_out), .sel({5{1'b1}}));
  BitSelector #(.width(32)) bitselector_3 (.in(SUB), .out(bitselector_3_out), .sel({5{1'b1}}));
  xor xor_1 (xor_1_out, bitselector_1_out, bitselector_2_out);
  xnor xnor_1 (xnor_1_out, bitselector_3_out, bitselector_2_out);
  and and_1 (SUB_O, xnor_1_out, xor_1_out);
  BitSelector #(.width(32), .group(5)) bitselector_4 (.in(SLL_X), .out(bitselector_4_out), .sel(3'b000));
  BitSelector #(.width(32), .group(5)) bitselector_5 (.in(SRL_X), .out(bitselector_5_out), .sel(3'b000));
  BitSelector #(.width(32), .group(5)) bitselector_6 (.in(SRA_X), .out(bitselector_6_out), .sel(3'b000));
  Comparator #(.width(32)) comparator_1 (.a(SLT_X), .b(SLT_Y), .eq(SLT_E), .lt(comparator_1_lt));  // open: gt
  assign SLT = comparator_1_lt ? 32'h1 : 32'bz;  // Controlled_Buffer controlled_buffer_1
  Shifter #(.width(32)) shifter_1 (.in(SLL_Y), .\dist (bitselector_4_out), .out(SLL));
  Shifter #(.width(32), .shift("lr")) shifter_2 (.in(SRL_Y), .\dist (bitselector_5_out), .out(SRL));
  Shifter #(.width(32), .shift("ar")) shifter_3 (.in(SRA_Y), .\dist (bitselector_6_out), .out(SRA));
  Adder #(.width(32)) adder_1 (.a(ADDU_X), .b(ADDU_Y), .out(ADDU));  // open: cin, cout
  not not_1 (not_1_out, comparator_1_lt);
  assign SLT = not_1_out ? {32{1'b0}} : 32'bz;  // Controlled_Buffer controlled_buffer_2
  BitSelector #(.width(32)) bitselector_7 (.in(ADD_X), .out(bitselector_7_out), .sel({5{1'b1}}));
  BitSelector #(.width(32)) bitselector_8 (.in(ADD_Y), .out(bitselector_8_out), .sel({5{1'b1}}));
  BitSelector #(.width(32)) bitselector_9 (.in(ADD), .out(bitselector_9_out), .sel({5{1'b1}}));
  Adder #(.width(32)) adder_2 (.a(ADD_Y), .b(ADD_X), .out(ADD));  // open: cin, cout
  and and_2 (and_2_out, bitselector_7_out, bitselector_8_out);
  not not_2 (not_2_out, bitselector_7_out);
  not not_3 (not_3_out, bitselector_8_out);
  not not_4 (not_4_out, bitselector_9_out);
  and and_3 (and_3_out, bitselector_9_out, and_4_out);
  and and_4 (and_4_out, not_2_out, not_3_out);
  Comparator #(.width(32), .mode("unsigned")) comparator_2 (
    .a(SLTU_X), .b(SLTU_Y), .eq(SLTU_E), .lt(comparator_2_lt));  // open: gt
  assign SLTU = comparator_2_lt ? 32'h1 : 32'bz;  // Controlled_Buffer controlled_buffer_3
  and and_5 (and_5_out, not_4_out, and_2_out);
  assign AND = AND_X & AND_Y;  // AND_Gate and_6, 32 bits wide
  assign OR = OR_X | OR_Y;  // OR_Gate or_1, 32 bits wide
  assign XOR = XOR_X ^ XOR_Y;  // XOR_Gate xor_2, 32 bits wide
  Subtractor #(.width(32)) subtractor_2 (.a(SUBU_X), .b(SUBU_Y), .out(SUBU));  // open: bin, bout
  not not_5 (not_5_out, comparator_2_lt);
  xor xor_3 (ADD_O, and_5_out, and_3_out);
  assign SLTU = not_5_out ? {32{1'b0}} : 32'bz;  // Controlled_Buffer controlled_buffer_4

  // Other names for the same wires on the sheet: overflow = Signed_Overflow; S[3:0] = Switch

  // Notes on the sheet:
  //   INPUTS to your circuit
  //   DON'T CHANGE THE LOCATIONS OF THE INPUTS AND OUTPUTS!
  //   OUTPUTS from your circuit
  //   SLL
  //   SRL
  //   SRA
  //   ADDU
  //   SLT
  //   AND
  //   OR
  //   XOR
  //   SUBU
  //   SLTU
endmodule
